// Logisim project ex4.circ as structural Verilog: 1 circuit, main circuit Split
module Split (
  input  [7:0] In1,
  output Out1,
  output [7:0] Out2
);


  // Notes on the sheet:
  //   PUT CIRCUITRY HERE
endmodule
